# Fritzing sketch LLRFNanoCar (saved by Fritzing 0.9.3b)
breadboards: 1

parts:
  HC-SR04_Sensor_1 = HC-SR04 Ultrasonic Distance Sensor
  Part1 = Arduino Nano (Rev3.0) (ICSP)
  LED1 = smd LED [color="Red (633nm)" package="0603 [SMD]"]
  L298N1 = L298N DC motor driver
  M1 = DC Motor  # not connected
  M2 = DC Motor  # not connected
  Power_plug3 = Power plug

nets:
  N1: HC-SR04_Sensor_1.VCC, LED1.cathode
  N2: HC-SR04_Sensor_1.TRIG, Part1.D4
  N3: HC-SR04_Sensor_1.ECHO, Part1.D5
  GND: HC-SR04_Sensor_1.GND, L298N1.GND, Power_plug3.GND
  N4: Part1.D2, L298N1.IN1
  N5: Part1.D3, L298N1.ENA
  N6: Part1.D6, L298N1.ENB
  N7: Part1.D7, L298N1.IN2
  N8: Part1.D8, L298N1.IN3
  5V: Part1.5V, L298N1.5V
  N9: Part1.A2, L298N1.IN4
  12V: L298N1.12V, Power_plug3.VCC

custom parts:
  L298N DC motor driver: 2x DC motor driver with 78M05 positive voltage regulator (7..35 V) L298N: max 46 V, 2 A Set 5 V Enable jumper to enable 5 V regultor (needed for the L298N) and +5 V output at screw terminal or supply external +5 V at screw terminal Set ENA and/or ENB to +5 V to enable motor permanently or supply ENA and/or ENB with PWM signal IN1 and IN2 set rotation directory for motor A (OUT1/OUT2) IN2 and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

// code stored in the sketch: LLRFNanocar.ino
//////////////importing libraries////////////////////////////////
#include <SPI.h> //communication protocol
#include <nRF24L01.h> //communication using radio waves to send and recieve data
#include <RF24.h>
#include "SR04.h"

//defining pins for ultrasonic sensor (looks like two speakers and measures distance)
#define TRIG_PIN 4
#define ECHO_PIN 5
SR04 sr04 = SR04(ECHO_PIN,TRIG_PIN);
long a;
unsigned long lastUltraRead = 0;
const unsigned long ULTRA_INTERVAL = 60; // ms

#define warnLED A0

RF24 radio(10, 9); // CE, CSN
const byte address[6] = "00001"; // the address the the module
///pins D10,D9,D13,D4,D5 : DO NOT USE THESE PINS
#include <Servo.h>

/* Motor A connections: 
in1 and in2 pins are used to control the direction of Motor A
connected to pin 13, pin 12 */
int enA = 3; 
int in1 = 2; 
int in2 = 7;
/* Motor B connections: 
in3 and in4 pins are used to control the direction of Motor B
connected to pin 11, pin 10 */
int enB = 6; 
int in3 = 8; 
int in4 = A2; 



void setup() {
  Serial.begin(9600);
  
  radio.begin();
  radio.openReadingPipe(0, address);
  radio.setPALevel(RF24_PA_MAX);
  radio.startListening();

  pinMode(warnLED, OUTPUT);
  digitalWrite(warnLED, LOW);
  delay(50);
  digitalWrite(warnLED, HIGH);
  delay(50);
  digitalWrite(warnLED, LOW);
  delay(50);
  digitalWrite(warnLED, HIGH);
  delay(50);
  digitalWrite(warnLED, LOW);

// pins initiation
    pinMode(enA, OUTPUT);
    pinMode(enB, OUTPUT);
    pinMode(in1, OUTPUT);
    pinMode(in2, OUTPUT);
    pinMode(in3, OUTPUT);
    pinMode(in4, OUTPUT);

    digitalWrite(in1, LOW);
    digitalWrite(in2, LOW);
    digitalWrite(in3, LOW);
    digitalWrite(in4, LOW);

    delay(1000);
    initDrive(80);

}

void loop() {
  if (radio.available()) {
    int receivedData[2];
    radio.read(&receivedData, sizeof(receivedData));

    int joyposV = receivedData[0];
    int joyposH = receivedData[1];

    int decLim = 300;
    int incLim = 700;

    float speedLim = 0.5; //50%

    int driveD = map(joyposV, decLim, 0, 80, 255)*speedLim;
    int driveB = map(joyposV, incLim, 1023, 80, 255)*speedLim;

    int driveR = map(joyposH, incLim, 0, 80, 255)*speedLim;
    int driveL = map(joyposH, incLim, 1023, 80, 150)*speedLim;

    Serial.print(joyposV);
    Serial.print("  |  ");
    Serial.print(driveD);
    Serial.print("  |  ");
    Serial.print(driveB);
    Serial.print("  |||  ");
    Serial.print(joyposH);
    Serial.print("  |  ");
    Serial.print(driveL);
    Serial.print("  |  ");
    Serial.println(driveR);


//Forward and Back
  if(joyposV<decLim){
    //map then drive forwards
    analogWrite(enA, driveD);
    analogWrite(enB, driveD);
  
    // motor A CW ^ (forward)
    digitalWrite(in1, HIGH);
    digitalWrite(in2, LOW);
    // motor B CW ^ (forward)
    digitalWrite(in3, HIGH);
    digitalWrite(in4, LOW);
    }else if(joyposV>incLim){
      //moves back
    analogWrite(enA, driveB);
    analogWrite(enB, driveB);
   // motor A CCW (backwards)
    digitalWrite(in1, LOW);
    digitalWrite(in2, HIGH);
    // motor B CCW (backwards)
    digitalWrite(in3, LOW);
    digitalWrite(in4, HIGH);
  } else{
    // Turn off motors
    digitalWrite(in1, LOW);
    digitalWrite(in2, LOW);
    digitalWrite(in3, LOW);
    digitalWrite(in4, LOW);
  }

//Rotation
  if(joyposH<decLim){
    //rot R
    analogWrite(enA, driveR);
    analogWrite(enB, driveR);
  
    // motor A CCW
    digitalWrite(in1, LOW);
    digitalWrite(in2, HIGH);

    // motor B CW ^
    digitalWrite(in3, HIGH);
    digitalWrite(in4, LOW);
    } else if(joyposH>incLim){
      //rot L
    analogWrite(enA, driveL);
    analogWrite(enB, driveL);
  
   // motor A CW ^ 
    digitalWrite(in1, HIGH);
    digitalWrite(in2, LOW);

    // motor B CCW 
    digitalWrite(in3, LOW);
    digitalWrite(in4, HIGH);
    }

//////////////ULTRASOUND///////////////
    if (millis() - lastUltraRead >= ULTRA_INTERVAL) {
      lastUltraRead = millis();
      a = sr04.Distance();
    }
    Serial.print(a);
    Serial.println("cm");

    if(a<40 && a>20){ 
    digitalWrite(warnLED, HIGH);
    }else if(a<20){
      signal();
      

    }
    else{
    digitalWrite(warnLED, LOW);
    

    }
  }
}

/////////////////////////////////////////////////

void initDrive(int s){
  analogWrite(enA, s);
  analogWrite(enB, s);
 
  // motor A CW ^ (backwards)
    digitalWrite(in1, HIGH);
    digitalWrite(in2, LOW);
    // digitalWrite(in1, LOW);
    // digitalWrite(in2, HIGH);
    
  // motor B CW ^ (backwards)
    digitalWrite(in3, HIGH);
    digitalWrite(in4, LOW);

    delay(100);

 // Turn off motors
    digitalWrite(in1, LOW);
    digitalWrite(in2, LOW);
    digitalWrite(in3, LOW);
    digitalWrite(in4, LOW);
    delay(500);


 // motor A CCW (foawrds)
  digitalWrite(in1, LOW);
  digitalWrite(in2, HIGH);
  // digitalWrite(in1, HIGH);
  // digitalWrite(in2, LOW);

  // motor B CCW (foawrds)
    digitalWrite(in3, LOW);
    digitalWrite(in4, HIGH);
    delay(200);

 // Turn off motors
    digitalWrite(in1, LOW);
    digitalWrite(in2, LOW);
    digitalWrite(in3, LOW);
    digitalWrite(in4, LOW);
    delay(1000);

}


//FUNCTIONS////////////
void signal(){

  // Turn off motors
    digitalWrite(in1, LOW);
    digitalWrite(in2, LOW);
    digitalWrite(in3, LOW);
    digitalWrite(in4, LOW);
    delay(200);

  digitalWrite(warnLED, HIGH);
  delay(50);
  digitalWrite(warnLED, LOW);
  delay(50);
  digitalWrite(warnLED, HIGH);
  delay(50);
  digitalWrite(warnLED, LOW);
  delay(50);
  digitalWrite(warnLED, HIGH);
  delay(50);
  digitalWrite(warnLED, LOW);
  delay(50);
  digitalWrite(warnLED, HIGH);
  delay(50);
  digitalWrite(warnLED, LOW);
  delay(50);
  digitalWrite(warnLED, HIGH);
  delay(50);
  digitalWrite(warnLED, LOW);
  delay(50);
  digitalWrite(warnLED, HIGH);

  
  analogWrite(enA, 70);
  analogWrite(enB, 70);
 
  // motor A CW ^ (backwards)
    digitalWrite(in1, HIGH);
    digitalWrite(in2, LOW);
    // digitalWrite(in1, LOW);
    // digitalWrite(in2, HIGH);
    
  // motor B CW ^ (backwards)
    digitalWrite(in3, HIGH);
    digitalWrite(in4, LOW);

    delay(200);
}
